// Logisim project hw4.circ as structural Verilog: 7 circuits, main circuit main
module main (
);

  RAM ram_1 ();  // open: addr, data, sel, clk, ld, clr
  tedi_regfile tedi_regfile_1 ();  // open: rd, data_in, reset, clk, write_enable, rs1, rs2, out_8, out_9
  ROM rom_1 ();  // open: addr, data
  tedi_ALU tedi_alu_1 ();  // open: A, B, optype, data_out
endmodule

module tedi_adder (
  input  sub,
  input  [15:0] A,
  input  [15:0] B,
  output ovf,
  output [15:0] result
);

  wire one_bit_add_1_out, one_bit_add_2_out, one_bit_add_3_out, one_bit_add_4_out, one_bit_add_5_out,
       one_bit_add_6_out, one_bit_add_7_out, one_bit_add_8_out, one_bit_add_9_out, one_bit_add_10_out,
       one_bit_add_11_out, one_bit_add_12_out, one_bit_add_13_out, one_bit_add_14_out, one_bit_add_15_out,
       one_bit_add_16_out, xor_1_out, xor_2_out, xor_3_out, xor_4_out, xor_5_out, xor_6_out, xor_7_out,
       xor_8_out, xor_9_out, xor_10_out, xor_11_out, xor_12_out, xor_13_out, xor_14_out, xor_15_out,
       xor_16_out;

  one_bit_add one_bit_add_1 (
    .a(xor_1_out), .b(B[15]), .out(one_bit_add_1_out), .in(one_bit_add_2_out), .sum(result[15]));
  xor xor_1 (xor_1_out, A[15], sub);
  xor xor_2 (xor_2_out, A[14], sub);
  one_bit_add one_bit_add_2 (
    .a(xor_2_out), .b(B[14]), .out(one_bit_add_2_out), .in(one_bit_add_3_out), .sum(result[14]));
  xor xor_3 (xor_3_out, A[13], sub);
  one_bit_add one_bit_add_3 (
    .a(xor_3_out), .b(B[13]), .out(one_bit_add_3_out), .in(one_bit_add_4_out), .sum(result[13]));
  one_bit_add one_bit_add_4 (
    .a(xor_4_out), .b(B[12]), .out(one_bit_add_4_out), .in(one_bit_add_5_out), .sum(result[12]));
  xor xor_4 (xor_4_out, A[12], sub);
  one_bit_add one_bit_add_5 (
    .a(xor_5_out), .b(B[11]), .out(one_bit_add_5_out), .in(one_bit_add_6_out), .sum(result[11]));
  xor xor_5 (xor_5_out, A[11], sub);
  one_bit_add one_bit_add_6 (
    .a(xor_6_out), .b(B[10]), .out(one_bit_add_6_out), .in(one_bit_add_7_out), .sum(result[10]));
  xor xor_6 (xor_6_out, A[10], sub);
  one_bit_add one_bit_add_7 (.a(xor_7_out), .b(B[9]), .out(one_bit_add_7_out), .in(one_bit_add_8_out), .sum(result[9]));
  xor xor_7 (xor_7_out, A[9], sub);
  one_bit_add one_bit_add_8 (.a(xor_8_out), .b(B[8]), .out(one_bit_add_8_out), .in(one_bit_add_9_out), .sum(result[8]));
  xor xor_8 (xor_8_out, A[8], sub);
  one_bit_add one_bit_add_9 (
    .a(xor_9_out), .b(B[7]), .out(one_bit_add_9_out), .in(one_bit_add_10_out), .sum(result[7]));
  xor xor_9 (xor_9_out, A[7], sub);
  one_bit_add one_bit_add_10 (
    .a(xor_10_out), .b(B[6]), .out(one_bit_add_10_out), .in(one_bit_add_11_out), .sum(result[6]));
  xor xor_10 (xor_10_out, A[6], sub);
  xor xor_11 (xor_11_out, A[5], sub);
  one_bit_add one_bit_add_11 (
    .a(xor_11_out), .b(B[5]), .out(one_bit_add_11_out), .in(one_bit_add_12_out), .sum(result[5]));
  one_bit_add one_bit_add_12 (
    .a(xor_12_out), .b(B[4]), .out(one_bit_add_12_out), .in(one_bit_add_13_out), .sum(result[4]));
  xor xor_12 (xor_12_out, A[4], sub);
  one_bit_add one_bit_add_13 (
    .a(xor_13_out), .b(B[3]), .out(one_bit_add_13_out), .in(one_bit_add_14_out), .sum(result[3]));
  xor xor_13 (xor_13_out, A[3], sub);
  one_bit_add one_bit_add_14 (
    .a(xor_14_out), .b(B[2]), .out(one_bit_add_14_out), .in(one_bit_add_15_out), .sum(result[2]));
  xor xor_14 (xor_14_out, A[2], sub);
  xor xor_15 (xor_15_out, A[1], sub);
  one_bit_add one_bit_add_15 (
    .a(xor_15_out), .b(B[1]), .out(one_bit_add_15_out), .in(one_bit_add_16_out), .sum(result[1]));
  xor xor_16 (xor_16_out, A[0], sub);
  one_bit_add one_bit_add_16 (.a(xor_16_out), .b(B[0]), .out(one_bit_add_16_out), .in(sub), .sum(result[0]));
  xor xor_17 (ovf, one_bit_add_1_out, one_bit_add_2_out);
endmodule

module one_bit_add (
  input  a,
  input  b,
  input  in,
  output out,
  output sum
);

  wire and_1_out, and_2_out, xor_1_out;

  and and_1 (and_1_out, b, a);
  xor xor_1 (xor_1_out, a, b);
  or or_1 (out, and_1_out, and_2_out);
  and and_2 (and_2_out, xor_1_out, in);
  xor xor_2 (sum, in, xor_1_out);
endmodule

module tedi_register (
  input  [15:0] data_in,
  input  reset,
  input  clk,
  input  write_enable,
  output [15:0] data_out
);

  wire and_1_out;

  and and_1 (and_1_out, clk, write_enable);
  D_Flip_Flop d_ff_1 (.D(data_in[0]), .clk(and_1_out), .Q(data_out[0]), .reset(reset));  // open: Qn, preset
  D_Flip_Flop d_ff_2 (.D(data_in[1]), .clk(and_1_out), .Q(data_out[1]), .reset(reset));  // open: Qn, preset
  D_Flip_Flop d_ff_3 (.D(data_in[2]), .clk(and_1_out), .Q(data_out[2]), .reset(reset));  // open: Qn, preset
  D_Flip_Flop d_ff_4 (.D(data_in[3]), .clk(and_1_out), .Q(data_out[3]), .reset(reset));  // open: Qn, preset
  D_Flip_Flop d_ff_5 (.D(data_in[4]), .clk(and_1_out), .Q(data_out[4]), .reset(reset));  // open: Qn, preset
  D_Flip_Flop d_ff_6 (.D(data_in[5]), .clk(and_1_out), .Q(data_out[5]), .reset(reset));  // open: Qn, preset
  D_Flip_Flop d_ff_7 (.D(data_in[6]), .clk(and_1_out), .Q(data_out[6]), .reset(reset));  // open: Qn, preset
  D_Flip_Flop d_ff_8 (.D(data_in[7]), .clk(and_1_out), .Q(data_out[7]), .reset(reset));  // open: Qn, preset
  D_Flip_Flop d_ff_9 (.D(data_in[8]), .clk(and_1_out), .Q(data_out[8]), .reset(reset));  // open: Qn, preset
  D_Flip_Flop d_ff_10 (.D(data_in[9]), .clk(and_1_out), .Q(data_out[9]), .reset(reset));  // open: Qn, preset
  D_Flip_Flop d_ff_11 (.D(data_in[10]), .clk(and_1_out), .Q(data_out[10]), .reset(reset));  // open: Qn, preset
  D_Flip_Flop d_ff_12 (.D(data_in[11]), .clk(and_1_out), .Q(data_out[11]), .reset(reset));  // open: Qn, preset
  D_Flip_Flop d_ff_13 (.D(data_in[12]), .clk(and_1_out), .Q(data_out[12]), .reset(reset));  // open: Qn, preset
  D_Flip_Flop d_ff_14 (.D(data_in[13]), .clk(and_1_out), .Q(data_out[13]), .reset(reset));  // open: Qn, preset
  D_Flip_Flop d_ff_15 (.D(data_in[14]), .clk(and_1_out), .Q(data_out[14]), .reset(reset));  // open: Qn, preset
  D_Flip_Flop d_ff_16 (.D(data_in[15]), .clk(and_1_out), .Q(data_out[15]), .reset(reset));  // open: Qn, preset

  // Other names for the same wires on the sheet: bit8 = data_in[8]; bit9 = data_in[9]; bit10 = data_in[10];
  //   bit11 = data_in[11]; bit12 = data_in[12]; bit13 = data_in[13]; bit14 = data_in[14]; bit15 = data_in[15]
endmodule

module tedi_regfile (
  input  [2:0] rd,
  input  [15:0] data_in,
  input  reset,
  input  [2:0] rs1,
  input  clk,
  input  write_enable,
  input  [2:0] rs2,
  output [15:0] out_8,
  output [15:0] out_9
);

  wire reg1, reg2, reg3, reg4, reg5, reg6, reg7;
  wire [15:0] out_reg1, out_reg2, out_reg3, out_reg4, out_reg5, out_reg6, out_reg7;

  Decoder #(.select(3)) decoder_1 (
    .out1(reg1), .out2(reg2), .out3(reg3), .out4(reg4), .out5(reg5), .out6(reg6), .out7(reg7), .sel(rd),
    .en(write_enable));  // open: out0
  tedi_register tedi_register_1 (.data_in(data_in), .reset(reset), .clk(clk), .write_enable(reg1), .data_out(out_reg1));
  tedi_register tedi_register_2 (.data_in(data_in), .reset(reset), .clk(clk), .write_enable(reg2), .data_out(out_reg2));
  tedi_register tedi_register_3 (.data_in(data_in), .reset(reset), .clk(clk), .write_enable(reg3), .data_out(out_reg3));
  tedi_register tedi_register_4 (.data_in(data_in), .reset(reset), .clk(clk), .write_enable(reg4), .data_out(out_reg4));
  tedi_register tedi_register_5 (.data_in(data_in), .reset(reset), .clk(clk), .write_enable(reg5), .data_out(out_reg5));
  tedi_register tedi_register_6 (.data_in(data_in), .reset(reset), .clk(clk), .write_enable(reg6), .data_out(out_reg6));
  tedi_register tedi_register_7 (.data_in(data_in), .reset(reset), .clk(clk), .write_enable(reg7), .data_out(out_reg7));
  Multiplexer #(.select(3), .width(16), .enable("false")) multiplexer_1 (
    .in0({16{1'b0}}), .in1(out_reg1), .in2(out_reg2), .in3(out_reg3), .in4(out_reg4), .in5(out_reg5),
    .in6(out_reg6), .in7(out_reg7), .out(out_8), .sel(rs1));
  Multiplexer #(.select(3), .width(16), .enable("false")) multiplexer_2 (
    .in0({16{1'b0}}), .in1(out_reg1), .in2(out_reg2), .in3(out_reg3), .in4(out_reg4), .in5(out_reg5),
    .in6(out_reg6), .in7(out_reg7), .out(out_9), .sel(rs2));
endmodule

module tedi_ALU (
  input  [15:0] A,
  input  [15:0] B,
  input  [2:0] optype,
  output [15:0] data_out
);

  wire [15:0] and_1_out, not_1_out, or_1_out, tedi_adder_1_result;

  tedi_adder tedi_adder_1 (.A(A), .B(B), .sub(optype[0]), .result(tedi_adder_1_result));  // open: ovf
  assign or_1_out = A | B;  // OR_Gate or_1, 16 bits wide
  assign and_1_out = A & B;  // AND_Gate and_1, 16 bits wide
  assign not_1_out = ~A;  // NOT_Gate not_1, 16 bits wide
  Multiplexer #(.select(3), .width(16), .enable("false")) multiplexer_1 (
    .in0(tedi_adder_1_result), .in1(tedi_adder_1_result), .in2(or_1_out), .in3(and_1_out), .in6(not_1_out),
    .out(data_out), .sel(optype));  // open: in4, in5, in7

  // Other names for the same wires on the sheet: sub = optype[0]

  // Notes on the sheet:
  //   001 - subtract
  //   010 - or
  //   011 - and
  //   000 - add
  //   110 - not A
  //   101 - left shift A with B
  //   100 - righst shift A with B
endmodule

module tedi_left_shifter (
  input  [15:0] data_input,
  input  [3:0] shift_amount,
  output [15:0] out
);

  wire multiplexer_1_out, multiplexer_2_out, multiplexer_3_out, multiplexer_4_out, multiplexer_5_out,
       multiplexer_6_out, multiplexer_7_out, multiplexer_8_out, multiplexer_9_out, multiplexer_10_out,
       multiplexer_11_out, multiplexer_12_out, multiplexer_13_out, multiplexer_14_out, multiplexer_15_out,
       multiplexer_16_out, multiplexer_17_out, multiplexer_18_out, multiplexer_19_out, multiplexer_20_out,
       multiplexer_21_out, multiplexer_22_out, multiplexer_23_out, multiplexer_24_out, multiplexer_25_out,
       multiplexer_26_out, multiplexer_27_out, multiplexer_28_out, multiplexer_29_out, multiplexer_30_out,
       multiplexer_31_out, multiplexer_32_out, multiplexer_33_out, multiplexer_34_out, multiplexer_35_out,
       multiplexer_36_out, multiplexer_37_out, multiplexer_38_out, multiplexer_39_out, multiplexer_40_out,
       multiplexer_41_out, multiplexer_42_out, multiplexer_43_out, multiplexer_44_out, multiplexer_45_out,
       multiplexer_46_out, multiplexer_47_out, multiplexer_48_out, shift0, shift1, shift2, shift3;

  Multiplexer #(.enable("false")) multiplexer_1 (
    .in0(data_input[15]), .in1(data_input[14]), .out(multiplexer_1_out), .sel(shift3));
  Multiplexer #(.enable("false")) multiplexer_2 (
    .in0(data_input[14]), .in1(data_input[13]), .out(multiplexer_2_out), .sel(shift3));
  Multiplexer #(.enable("false")) multiplexer_3 (
    .in0(data_input[13]), .in1(data_input[12]), .out(multiplexer_3_out), .sel(shift3));
  Multiplexer #(.enable("false")) multiplexer_4 (
    .in0(data_input[12]), .in1(data_input[11]), .out(multiplexer_4_out), .sel(shift3));
  Multiplexer #(.enable("false")) multiplexer_5 (
    .in0(data_input[11]), .in1(data_input[10]), .out(multiplexer_5_out), .sel(shift3));
  Multiplexer #(.enable("false")) multiplexer_6 (
    .in0(data_input[10]), .in1(data_input[9]), .out(multiplexer_6_out), .sel(shift3));
  Multiplexer #(.enable("false")) multiplexer_7 (
    .in0(data_input[9]), .in1(data_input[8]), .out(multiplexer_7_out), .sel(shift3));
  Multiplexer #(.enable("false")) multiplexer_8 (
    .in0(data_input[8]), .in1(data_input[7]), .out(multiplexer_8_out), .sel(shift3));
  Multiplexer #(.enable("false")) multiplexer_9 (
    .in0(data_input[7]), .in1(data_input[6]), .out(multiplexer_9_out), .sel(shift3));
  Multiplexer #(.enable("false")) multiplexer_10 (
    .in0(data_input[6]), .in1(data_input[5]), .out(multiplexer_10_out), .sel(shift3));
  Multiplexer #(.enable("false")) multiplexer_11 (
    .in0(data_input[5]), .in1(data_input[4]), .out(multiplexer_11_out), .sel(shift3));
  Multiplexer #(.enable("false")) multiplexer_12 (
    .in0(data_input[4]), .in1(data_input[3]), .out(multiplexer_12_out), .sel(shift3));
  Multiplexer #(.enable("false")) multiplexer_13 (
    .in0(data_input[3]), .in1(data_input[2]), .out(multiplexer_13_out), .sel(shift3));
  Multiplexer #(.enable("false")) multiplexer_14 (
    .in0(data_input[2]), .in1(data_input[1]), .out(multiplexer_14_out), .sel(shift3));
  Multiplexer #(.enable("false")) multiplexer_15 (
    .in0(data_input[1]), .in1(data_input[0]), .out(multiplexer_15_out), .sel(shift3));
  Multiplexer #(.enable("false")) multiplexer_16 (
    .in0(data_input[0]), .in1(1'b0), .out(multiplexer_16_out), .sel(shift3));
  Multiplexer #(.enable("false")) multiplexer_17 (
    .in0(multiplexer_1_out), .in1(multiplexer_2_out), .out(multiplexer_17_out), .sel(shift2));
  Multiplexer #(.enable("false")) multiplexer_18 (
    .in0(multiplexer_2_out), .in1(multiplexer_3_out), .out(multiplexer_18_out), .sel(shift2));
  Multiplexer #(.enable("false")) multiplexer_19 (
    .in0(multiplexer_3_out), .in1(multiplexer_4_out), .out(multiplexer_19_out), .sel(shift2));
  Multiplexer #(.enable("false")) multiplexer_20 (
    .in0(multiplexer_4_out), .in1(multiplexer_5_out), .out(multiplexer_20_out), .sel(shift2));
  Multiplexer #(.enable("false")) multiplexer_21 (
    .in0(multiplexer_5_out), .in1(multiplexer_6_out), .out(multiplexer_21_out), .sel(shift2));
  Multiplexer #(.enable("false")) multiplexer_22 (
    .in0(multiplexer_6_out), .in1(multiplexer_7_out), .out(multiplexer_22_out), .sel(shift2));
  Multiplexer #(.enable("false")) multiplexer_23 (
    .in0(multiplexer_7_out), .in1(multiplexer_8_out), .out(multiplexer_23_out), .sel(shift2));
  Multiplexer #(.enable("false")) multiplexer_24 (
    .in0(multiplexer_8_out), .in1(multiplexer_9_out), .out(multiplexer_24_out), .sel(shift2));
  Multiplexer #(.enable("false")) multiplexer_25 (
    .in0(multiplexer_9_out), .in1(multiplexer_10_out), .out(multiplexer_25_out), .sel(shift2));
  Multiplexer #(.enable("false")) multiplexer_26 (
    .in0(multiplexer_10_out), .in1(multiplexer_11_out), .out(multiplexer_26_out), .sel(shift2));
  Multiplexer #(.enable("false")) multiplexer_27 (
    .in0(multiplexer_11_out), .in1(multiplexer_12_out), .out(multiplexer_27_out), .sel(shift2));
  Multiplexer #(.enable("false")) multiplexer_28 (
    .in0(multiplexer_12_out), .in1(multiplexer_13_out), .out(multiplexer_28_out), .sel(shift2));
  Multiplexer #(.enable("false")) multiplexer_29 (
    .in0(multiplexer_13_out), .in1(multiplexer_14_out), .out(multiplexer_29_out), .sel(shift2));
  Multiplexer #(.enable("false")) multiplexer_30 (
    .in0(multiplexer_14_out), .in1(multiplexer_15_out), .out(multiplexer_30_out), .sel(shift2));
  Multiplexer #(.enable("false")) multiplexer_31 (
    .in0(multiplexer_15_out), .in1(multiplexer_16_out), .out(multiplexer_31_out), .sel(shift2));
  Multiplexer #(.enable("false")) multiplexer_32 (
    .in0(multiplexer_16_out), .in1(1'b0), .out(multiplexer_32_out), .sel(shift2));
  Multiplexer #(.enable("false")) multiplexer_33 (
    .in0(multiplexer_17_out), .in1(multiplexer_18_out), .out(multiplexer_33_out), .sel(shift1));
  Multiplexer #(.enable("false")) multiplexer_34 (
    .in0(multiplexer_18_out), .in1(multiplexer_19_out), .out(multiplexer_34_out), .sel(shift1));
  Multiplexer #(.enable("false")) multiplexer_35 (
    .in0(multiplexer_19_out), .in1(multiplexer_20_out), .out(multiplexer_35_out), .sel(shift1));
  Multiplexer #(.enable("false")) multiplexer_36 (
    .in0(multiplexer_20_out), .in1(multiplexer_21_out), .out(multiplexer_36_out), .sel(shift1));
  Multiplexer #(.enable("false")) multiplexer_37 (
    .in0(multiplexer_21_out), .in1(multiplexer_22_out), .out(multiplexer_37_out), .sel(shift1));
  Multiplexer #(.enable("false")) multiplexer_38 (
    .in0(multiplexer_22_out), .in1(multiplexer_23_out), .out(multiplexer_38_out), .sel(shift1));
  Multiplexer #(.enable("false")) multiplexer_39 (
    .in0(multiplexer_23_out), .in1(multiplexer_24_out), .out(multiplexer_39_out), .sel(shift1));
  Multiplexer #(.enable("false")) multiplexer_40 (
    .in0(multiplexer_24_out), .in1(multiplexer_25_out), .out(multiplexer_40_out), .sel(shift1));
  Multiplexer #(.enable("false")) multiplexer_41 (
    .in0(multiplexer_25_out), .in1(multiplexer_26_out), .out(multiplexer_41_out), .sel(shift1));
  Multiplexer #(.enable("false")) multiplexer_42 (
    .in0(multiplexer_26_out), .in1(multiplexer_27_out), .out(multiplexer_42_out), .sel(shift1));
  Multiplexer #(.enable("false")) multiplexer_43 (
    .in0(multiplexer_27_out), .in1(multiplexer_28_out), .out(multiplexer_43_out), .sel(shift1));
  Multiplexer #(.enable("false")) multiplexer_44 (
    .in0(multiplexer_28_out), .in1(multiplexer_29_out), .out(multiplexer_44_out), .sel(shift1));
  Multiplexer #(.enable("false")) multiplexer_45 (
    .in0(multiplexer_29_out), .in1(multiplexer_30_out), .out(multiplexer_45_out), .sel(shift1));
  Multiplexer #(.enable("false")) multiplexer_46 (
    .in0(multiplexer_30_out), .in1(multiplexer_31_out), .out(multiplexer_46_out), .sel(shift1));
  Multiplexer #(.enable("false")) multiplexer_47 (
    .in0(multiplexer_31_out), .in1(multiplexer_32_out), .out(multiplexer_47_out), .sel(shift1));
  Multiplexer #(.enable("false")) multiplexer_48 (
    .in0(multiplexer_32_out), .in1(1'b0), .out(multiplexer_48_out), .sel(shift1));
  Multiplexer #(.enable("false")) multiplexer_49 (
    .in0(multiplexer_33_out), .in1(multiplexer_34_out), .out(out[15]), .sel(shift0));
  Multiplexer #(.enable("false")) multiplexer_50 (
    .in0(multiplexer_34_out), .in1(multiplexer_35_out), .out(out[14]), .sel(shift0));
  Multiplexer #(.enable("false")) multiplexer_51 (
    .in0(multiplexer_35_out), .in1(multiplexer_36_out), .out(out[13]), .sel(shift0));
  Multiplexer #(.enable("false")) multiplexer_52 (
    .in0(multiplexer_36_out), .in1(multiplexer_37_out), .out(out[12]), .sel(shift0));
  Multiplexer #(.enable("false")) multiplexer_53 (
    .in0(multiplexer_37_out), .in1(multiplexer_38_out), .out(out[11]), .sel(shift0));
  Multiplexer #(.enable("false")) multiplexer_54 (
    .in0(multiplexer_38_out), .in1(multiplexer_39_out), .out(out[10]), .sel(shift0));
  Multiplexer #(.enable("false")) multiplexer_55 (
    .in0(multiplexer_39_out), .in1(multiplexer_40_out), .out(out[9]), .sel(shift0));
  Multiplexer #(.enable("false")) multiplexer_56 (
    .in0(multiplexer_40_out), .in1(multiplexer_41_out), .out(out[8]), .sel(shift0));
  Multiplexer #(.enable("false")) multiplexer_57 (
    .in0(multiplexer_41_out), .in1(multiplexer_42_out), .out(out[7]), .sel(shift0));
  Multiplexer #(.enable("false")) multiplexer_58 (
    .in0(multiplexer_42_out), .in1(multiplexer_43_out), .out(out[6]), .sel(shift0));
  Multiplexer #(.enable("false")) multiplexer_59 (
    .in0(multiplexer_43_out), .in1(multiplexer_44_out), .out(out[5]), .sel(shift0));
  Multiplexer #(.enable("false")) multiplexer_60 (
    .in0(multiplexer_44_out), .in1(multiplexer_45_out), .out(out[4]), .sel(shift0));
  Multiplexer #(.enable("false")) multiplexer_61 (
    .in0(multiplexer_45_out), .in1(multiplexer_46_out), .out(out[3]), .sel(shift0));
  Multiplexer #(.enable("false")) multiplexer_62 (
    .in0(multiplexer_46_out), .in1(multiplexer_47_out), .out(out[2]), .sel(shift0));
  Multiplexer #(.enable("false")) multiplexer_63 (
    .in0(multiplexer_47_out), .in1(multiplexer_48_out), .out(out[1]), .sel(shift0));
  Multiplexer #(.enable("false")) multiplexer_64 (.in0(multiplexer_48_out), .in1(1'b0), .out(out[0]), .sel(shift0));

  // Other names for the same wires on the sheet: bit0 = data_input[0]; bit1 = data_input[1]; bit2 = data_input[2];
  //   bit3 = data_input[3]; bit4 = data_input[4]; bit5 = data_input[5]; bit6 = data_input[6]; bit7 = data_input[7];
  //   bit8 = data_input[8]; bit9 = data_input[9]; bit10 = data_input[10]; bit11 = data_input[11];
  //   bit12 = data_input[12]; bit13 = data_input[13]; bit14 = data_input[14]; bit15 = data_input[15];
  //   shift_3 = shift_amount[0]; shift_2 = shift_amount[1]; shift_1 = shift_amount[2]; shift_0 = shift_amount[3]
endmodule
